# Fritzing sketch Schematics (saved by Fritzing 0.9.5d)
breadboards: 1

parts:
  Компонент1 = Arduino Uno (Rev3) - ICSP
  ACC_PIN_17_(BUS+) = female pin header, 1 pin [form="♀ (female)"]
  PIN_7_(GND) = female pin header, 1 pin [form="♀ (female)"]
  R1 = Resistor [tolerance=±5% resistance=220 package="0603 [SMD]"]
  D1 = Schottky Diode [part_number=1N5817 package="300 mil [THT]"]
  FRONT_PANEL_CHIP_15_(ROW) = female pin header, 1 pin [form="♀ (female)"]

nets:
  N1: Компонент1.D8, D1.cathode
  N2: Компонент1.D2, ACC_PIN_17_(BUS+).pin1
  N3: Компонент1.GND, PIN_7_(GND).pin1
  N4: R1.Pin_0, D1.anode
  N5: R1.Pin_1, FRONT_PANEL_CHIP_15_(ROW).pin1
